// Logisim project LAB-1.circ as structural Verilog: 4 circuits, main circuit main
module main (
  input  A,
  input  B,
  input  C,
  output F_A_prime_C_AB_prime_BC
);

  wire ic7404_1_out_8, ic7404_1_out_10, ic7408_1_out_13, ic7408_1_out_16, ic7408_1_out_17, ic_7432_1_out_17;

  Ic7404 ic7404_1 (
    .in_2(B), .in_4(A), .out_8(ic7404_1_out_8), .out_10(ic7404_1_out_10));  // open: in_1, in_3, in_5, in_6, out_7, out_9, out_11, out_12
  ic7408 ic7408_1 (
    .in_1(ic7404_1_out_10), .in_2(C), .in_7(A), .in_8(ic7404_1_out_8), .out_13(ic7408_1_out_13),
    .out_16(ic7408_1_out_16), .out_17(ic7408_1_out_17), .in_10(C), .in_9(B));  // open: in_3, in_4, in_5, in_6, out_14, out_15, in_11, out_18, in_12
  ic_7432 ic_7432_1 (
    .in_5(ic7408_1_out_17), .in_6(ic_7432_1_out_17), .in_9(ic7408_1_out_16), .in_10(ic7408_1_out_13),
    .out_15(F_A_prime_C_AB_prime_BC), .out_17(ic_7432_1_out_17));  // open: in_1, in_2, in_3, in_4, in_7, in_8, in_11, in_12, out_13, out_14, out_16, out_18

  // Notes on the sheet:
  //   B'
  //   NOT Gate
  //   AND Gate
  //   A'
  //   A'C
  //   AB'
  //   BC
  //   OR Gate
  //   A'C+AB'
endmodule

module ic7408 (
  input  in_1,
  input  in_2,
  input  in_3,
  input  in_4,
  input  in_5,
  input  in_6,
  input  in_7,
  input  in_8,
  input  in_9,
  input  in_10,
  input  in_11,
  input  in_12,
  output out_13,
  output out_14,
  output out_15,
  output out_16,
  output out_17,
  output out_18
);

  and and_1 (out_13, in_1, in_2);
  and and_2 (out_14, in_3, in_4);
  and and_3 (out_15, in_5, in_6);
  and and_4 (out_16, in_7, in_8);
  and and_5 (out_17, in_9, in_10);
  and and_6 (out_18, in_11, in_12);
endmodule

module Ic7404 (
  input  in_1,
  input  in_2,
  input  in_3,
  input  in_4,
  input  in_5,
  input  in_6,
  output out_7,
  output out_8,
  output out_9,
  output out_10,
  output out_11,
  output out_12
);

  not not_1 (out_7, in_1);
  not not_2 (out_8, in_2);
  not not_3 (out_9, in_3);
  not not_4 (out_10, in_4);
  not not_5 (out_11, in_5);
  not not_6 (out_12, in_6);
endmodule

module ic_7432 (
  input  in_1,
  input  in_2,
  input  in_3,
  input  in_4,
  input  in_5,
  input  in_6,
  input  in_7,
  input  in_8,
  input  in_9,
  input  in_10,
  input  in_11,
  input  in_12,
  output out_13,
  output out_14,
  output out_15,
  output out_16,
  output out_17,
  output out_18
);

  or or_1 (out_13, in_1, in_2);
  or or_2 (out_14, in_3, in_4);
  or or_3 (out_15, in_5, in_6);
  or or_4 (out_16, in_7, in_8);
  or or_5 (out_17, in_9, in_10);
  or or_6 (out_18, in_11, in_12);
endmodule
