// Logisim project LAB-3.circ as structural Verilog: 4 circuits, main circuit main
module main (
  input  A,
  input  B,
  input  C,
  input  A_2,
  input  B_2,
  input  C_2,
  output out_7,
  output out_8
);

  wire ic_4075_1_out_10, ic_4075_1_out_11, ic_4075_1_out_12, ic_4075_2_out_10, ic_4075_2_out_12,
       ic_7404_1_out_4, ic_7404_1_out_5, ic_7404_1_out_6, ic_7404_2_out_4, ic_7404_2_out_5, ic_7404_2_out_6,
       ic_7411_1_out_10, ic_7411_1_out_11, ic_7411_1_out_12, ic_7411_2_out_10;

  IC_7404 ic_7404_1 (
    .in_1(A), .in_2(B), .in_3(C), .out_4(ic_7404_1_out_4), .out_5(ic_7404_1_out_5), .out_6(ic_7404_1_out_6));
  IC_7404 ic_7404_2 (
    .in_1(A_2), .in_2(B_2), .in_3(C_2), .out_4(ic_7404_2_out_4), .out_5(ic_7404_2_out_5),
    .out_6(ic_7404_2_out_6));
  IC_7411 ic_7411_1 (
    .in_1(ic_7404_1_out_4), .in_2(ic_7404_1_out_5), .in_3(C), .in_4(A), .in_5(B), .in_6(ic_7404_1_out_6),
    .in_7(ic_7404_1_out_4), .in_8(B), .in_9(ic_7404_1_out_6), .out_10(ic_7411_1_out_10),
    .out_11(ic_7411_1_out_11), .out_12(ic_7411_1_out_12));
  IC_4075 ic_4075_1 (
    .in_1(A_2), .in_2(B_2), .in_3(C_2), .in_4(B_2), .in_5(C_2), .in_6(ic_7404_2_out_4), .in_7(A_2),
    .in_8(ic_7404_2_out_5), .in_9(ic_7404_2_out_6), .out_10(ic_4075_1_out_10), .out_11(ic_4075_1_out_11),
    .out_12(ic_4075_1_out_12));
  IC_4075 ic_4075_2 (
    .in_1(ic_7404_2_out_4), .in_2(B_2), .in_3(ic_7404_2_out_6), .in_7(ic_7404_2_out_4),
    .in_8(ic_7404_2_out_6), .in_9(ic_7404_2_out_5), .out_10(ic_4075_2_out_10), .out_12(ic_4075_2_out_12));  // open: in_4, in_5, in_6, out_11
  IC_4075 ic_4075_3 (
    .in_1(ic_7411_1_out_10), .in_2(ic_7411_1_out_12), .in_3(ic_7411_1_out_11), .out_10(out_7));  // open: in_4, in_5, in_6, in_7, in_8, in_9, out_11, out_12
  IC_7411 ic_7411_2 (
    .in_1(ic_4075_2_out_12), .in_2(ic_4075_2_out_10), .in_3(ic_4075_1_out_11), .in_7(ic_7411_2_out_10),
    .in_8(ic_4075_1_out_12), .in_9(ic_4075_1_out_10), .out_10(ic_7411_2_out_10), .out_12(out_8));  // open: in_4, in_5, in_6, out_11

  // Notes on the sheet:
  //   1'st canonical form
  //   2nd canonical form
  //   B'
  //   A'
  //   A'
  //   IC7404
  //   C'
  //   IC7404
  //   C'
  //   B'
  //   A+B+C
  //   A'B'C
  //   IC7411
  //   IC7411
  //   IC7411
  //   A'BC'
  //   IC4075
  //   A+B'+C'
  //   ABC'
  //   A'B'C+A'BC'+ABC'
  //   IC4075
  //   IC4075
  //   A'+B+C'
  //   A'+B+C
  //   (A'+B'+C').(A'+B+C').(A'+B+C).(A+B'+C').(A+B+C)
  //   A'+B'+C'
  //   (A'+B'+C').(A'+B+C').(A'+B+C)
  //   IC7411
endmodule

module IC_7411 (
  input  in_1,
  input  in_2,
  input  in_3,
  input  in_4,
  input  in_5,
  input  in_6,
  input  in_7,
  input  in_8,
  input  in_9,
  output out_10,
  output out_11,
  output out_12
);

  and and_1 (out_10, in_1, in_2, in_3);
  and and_2 (out_11, in_4, in_5, in_6);
  and and_3 (out_12, in_7, in_8, in_9);
endmodule

module IC_4075 (
  input  in_1,
  input  in_2,
  input  in_3,
  input  in_4,
  input  in_5,
  input  in_6,
  input  in_7,
  input  in_8,
  input  in_9,
  output out_10,
  output out_11,
  output out_12
);

  or or_1 (out_10, in_1, in_2, in_3);
  or or_2 (out_11, in_4, in_5, in_6);
  or or_3 (out_12, in_7, in_8, in_9);
endmodule

module IC_7404 (
  input  in_1,
  input  in_2,
  input  in_3,
  output out_4,
  output out_5,
  output out_6
);

  not not_1 (out_4, in_1);
  not not_2 (out_5, in_2);
  not not_3 (out_6, in_3);
endmodule
