// Logisim project LAB-4.circ as structural Verilog: 4 circuits, main circuit IC7408
module IC7408 (
  input  in_1,
  input  in_2,
  input  in_3,
  input  in_4,
  input  in_5,
  input  in_6,
  input  in_7,
  input  in_8,
  input  in_9,
  input  in_10,
  input  in_11,
  input  in_12,
  output out_13,
  output out_14,
  output out_15,
  output out_16
);

  and and_1 (out_13, in_1, in_2, in_3);
  and and_2 (out_14, in_4, in_5, in_6);
  and and_3 (out_15, in_7, in_8, in_9);
  and and_4 (out_16, in_10, in_11, in_12);
endmodule

module IC7432 (
  input  in_1,
  input  in_2,
  input  in_3,
  input  in_4,
  input  in_5,
  input  in_6,
  input  in_7,
  input  in_8,
  input  in_9,
  input  in_10,
  input  in_11,
  input  in_12,
  output out_13,
  output out_14,
  output out_15,
  output out_16
);

  or or_1 (out_13, in_1, in_2, in_3);
  or or_2 (out_14, in_4, in_5, in_6);
  or or_3 (out_15, in_7, in_8, in_9);
  or or_4 (out_16, in_10, in_11, in_12);
endmodule

module IC7404 (
  input  in_1,
  input  in_2,
  input  in_3,
  input  in_4,
  output out_5,
  output out_6,
  output out_7,
  output out_8
);

  not not_1 (out_5, in_1);
  not not_2 (out_6, in_2);
  not not_3 (out_7, in_3);
  not not_4 (out_8, in_4);
endmodule

module main (
  input  W,
  input  X,
  input  Y,
  input  Z,
  output A,
  output B,
  output C,
  output D
);

  wire IC7404_out_5, IC7404_out_7, IC7404_out_8, ic7408_1_out_13, ic7408_1_out_14, ic7408_1_out_15,
       ic7408_1_out_16, ic7408_2_out_13, ic7408_2_out_14, ic7408_2_out_16;

  IC7404 IC7404 (
    .in_1(X), .in_3(Z), .in_4(Y), .out_5(IC7404_out_5), .out_7(IC7404_out_7), .out_8(IC7404_out_8));  // open: in_2, out_6
  IC7408 ic7408_1 (
    .in_1(X), .in_2(Z), .in_3(Z), .in_4(IC7404_out_5), .in_5(Z), .in_6(Z), .in_7(IC7404_out_5), .in_8(Y),
    .in_9(Y), .in_10(X), .in_11(Y), .in_12(Y), .out_13(ic7408_1_out_13), .out_14(ic7408_1_out_14),
    .out_15(ic7408_1_out_15), .out_16(ic7408_1_out_16));
  IC7408 ic7408_2 (
    .in_1(X), .in_2(IC7404_out_8), .in_3(IC7404_out_7), .in_4(Z), .in_5(Z), .in_6(Y), .in_10(IC7404_out_8),
    .in_11(IC7404_out_7), .in_12(IC7404_out_7), .out_13(ic7408_2_out_13), .out_14(ic7408_2_out_14),
    .out_16(ic7408_2_out_16));  // open: in_7, in_8, in_9, out_15
  IC7432 IC7432 (
    .in_1(W), .in_2(ic7408_1_out_16), .in_3(ic7408_1_out_13), .in_4(ic7408_2_out_14), .in_5(ic7408_2_out_16),
    .in_6(ic7408_2_out_16), .in_7(IC7404_out_7), .in_8(IC7404_out_7), .in_9(IC7404_out_7),
    .in_10(ic7408_1_out_14), .in_11(ic7408_1_out_15), .in_12(ic7408_2_out_13), .out_13(A), .out_14(C),
    .out_15(D), .out_16(B));

  // Notes on the sheet:
  //   X'
  //   Y'
  //   Z'
  //   Y'Z'
  //   XY
  //   IC7408
  //   IC7408
  //   XZ
  //   YZ
  //   X'Z
  //   X'Y
  //   XY'Z'
  //   W
endmodule
