// Logisim project LAB-5.circ as structural Verilog: 5 circuits, main circuit main
module main (
  input  A3,
  input  A2,
  input  A1,
  input  A0,
  input  Controler,
  input  B3,
  input  B2,
  input  B1,
  input  B0,
  input  A3_2,
  input  A2_2,
  input  A1_2,
  input  A0_2,
  input  B3_2,
  input  B2_2,
  input  B1_2,
  input  B0_2,
  input  in_18,
  output [4:0] out_19,
  output [3:0] out_20
);

  wire ic7408_1_out_9, ic7408_1_out_10, ic7432_1_out_9, ic7432_1_out_10, ic7486_1_out_9, ic7486_1_out_10,
       ic7486_1_out_11, ic7486_1_out_12, ic74283_1_out_14, ic74283_1_s1, ic74283_1_s2, ic74283_1_s3,
       ic74283_1_s4, ic74283_2_out_14;

  IC7486 ic7486_1 (
    .in_1(B3), .in_2(Controler), .in_3(B2), .in_4(Controler), .in_5(B1), .in_6(Controler), .in_7(B0),
    .in_8(Controler), .out_9(ic7486_1_out_9), .out_10(ic7486_1_out_10), .out_11(ic7486_1_out_11),
    .out_12(ic7486_1_out_12));
  IC74283 ic74283_1 (
    .A0(A0_2), .B0(B0_2), .A1(A1_2), .B1(B1_2), .A2(A2_2), .B2(B2_2), .A3(A3_2), .B3(B3_2),
    .S1(ic74283_1_s1), .S2(ic74283_1_s2), .S3(ic74283_1_s3), .S4(ic74283_1_s4), .out_14(ic74283_1_out_14));  // open: in_1
  IC74283 ic74283_2 (
    .A0(in_18), .B0(ic74283_1_s1), .A1(ic7432_1_out_10), .B1(ic74283_1_s2), .A2(ic7432_1_out_10),
    .B2(ic74283_1_s3), .A3(in_18), .B3(ic74283_1_s4), .S1(out_20[0]), .S2(out_20[1]), .S3(out_20[2]),
    .S4(out_20[3]), .out_14(ic74283_2_out_14));  // open: in_1
  IC74283 ic74283_3 (
    .A0(A0), .B0(ic7486_1_out_12), .A1(A1), .B1(ic7486_1_out_11), .A2(A2), .B2(ic7486_1_out_10), .A3(A3),
    .B3(ic7486_1_out_9), .S1(out_19[0]), .S2(out_19[1]), .S3(out_19[2]), .S4(out_19[3]), .out_14(out_19[4]),
    .in_1(Controler));
  IC7408 ic7408_1 (
    .in_1(ic74283_1_s4), .in_2(ic74283_1_s3), .in_3(ic74283_1_s4), .in_4(ic74283_1_s2),
    .out_9(ic7408_1_out_9), .out_10(ic7408_1_out_10));  // open: in_5, in_6, in_7, in_8, out_11, out_12
  IC7432 ic7432_1 (
    .in_1(ic7408_1_out_9), .in_2(ic7408_1_out_10), .in_3(ic7432_1_out_9), .in_4(ic74283_1_out_14),
    .out_9(ic7432_1_out_9), .out_10(ic7432_1_out_10));  // open: in_5, in_6, in_7, in_8, out_11, out_12

  // Notes on the sheet:
  //   IC7486
  //   C.out
  //   S3
  //   S1
  //   IC74283
  //   S4
  //   S2
endmodule

module IC74283 (
  input  in_1,
  input  A0,
  input  B0,
  input  A1,
  input  B1,
  input  A2,
  input  B2,
  input  A3,
  input  B3,
  output S1,
  output S2,
  output S3,
  output S4,
  output out_14
);

  wire adder_1_cout, adder_2_cout, adder_3_cout;

  Adder #(.width(1)) adder_1 (.a(A0), .b(B0), .out(S1), .cin(in_1), .cout(adder_1_cout));
  Adder #(.width(1)) adder_2 (.a(A1), .b(B1), .out(S2), .cin(adder_1_cout), .cout(adder_2_cout));
  Adder #(.width(1)) adder_3 (.a(A2), .b(B2), .out(S3), .cin(adder_2_cout), .cout(adder_3_cout));
  Adder #(.width(1)) adder_4 (.a(A3), .b(B3), .out(S4), .cin(adder_3_cout), .cout(out_14));
endmodule

module IC7486 (
  input  in_1,
  input  in_2,
  input  in_3,
  input  in_4,
  input  in_5,
  input  in_6,
  input  in_7,
  input  in_8,
  output out_9,
  output out_10,
  output out_11,
  output out_12
);

  xor xor_1 (out_9, in_1, in_2);
  xor xor_2 (out_10, in_3, in_4);
  xor xor_3 (out_11, in_5, in_6);
  xor xor_4 (out_12, in_7, in_8);
endmodule

module IC7408 (
  input  in_1,
  input  in_2,
  input  in_3,
  input  in_4,
  input  in_5,
  input  in_6,
  input  in_7,
  input  in_8,
  output out_9,
  output out_10,
  output out_11,
  output out_12
);

  and and_1 (out_9, in_1, in_2);
  and and_2 (out_10, in_3, in_4);
  and and_3 (out_11, in_5, in_6);
  and and_4 (out_12, in_7, in_8);
endmodule

module IC7432 (
  input  in_1,
  input  in_2,
  input  in_3,
  input  in_4,
  input  in_5,
  input  in_6,
  input  in_7,
  input  in_8,
  output out_9,
  output out_10,
  output out_11,
  output out_12
);

  or or_1 (out_9, in_1, in_2);
  or or_2 (out_10, in_3, in_4);
  or or_3 (out_11, in_5, in_6);
  or or_4 (out_12, in_7, in_8);
endmodule
